# Fritzing sketch receiver (saved by Fritzing 0.9.6b)
circuit board: 8.46667cm x 5.64444cm

parts:
  Part1 = Arduino Nano (Rev3.0)
  Part2 = NRF24L01+ Breakout Board
  U1 = LCD-16X2 [package=lcd-16x2]
  U2 = POT [package=pot_alpha_rv16af-20]
  LED1 = smd LED [color="Red (633nm)" package="0805 [SMD]"]

nets:
  N1: Part1.D0/RX, U1.R_W
  GND: Part1.GND, Part2.GND, U1.VSS, U1.K, U2.E, LED1.cathode
  N2: Part1.D2, LED1.anode
  N3: Part1.D3, U1.RS
  N4: Part1.D4, U1.E
  N5: Part1.D5, U1.DB4
  N6: Part1.D6, U1.DB5
  N7: Part1.D7, U1.DB6
  N8: Part1.D8, U1.DB7
  N9: Part1.D9, Part2.CE
  N10: Part1.D10, Part2.CS
  N11: Part1.D11/MOSI, Part2.MOSI
  N12: Part1.D12/MISO, Part2.MISO
  5V: Part1.5V, U1.VDD, U1.A, U2.A
  3V3: Part1.3V3, Part2.VCC
  N13: Part1.D13/SCK, Part2.SCK
  N14: U1.VO, U2.S
