# Fritzing sketch transmitter (saved by Fritzing 0.9.6b)
circuit board: 8.46667cm x 5.64444cm

parts:
  Part1 = Arduino Nano (Rev3.0)
  Part2 = NRF24L01+ Breakout Board
  LED1 = smd LED [color="Red (633nm)" package="0805 [SMD]"]
  SG1 = Buzzer 12mm [package=buzzer-12mm-ns]

nets:
  GND: Part1.GND, Part2.GND, LED1.cathode, SG1.1
  N1: Part1.D2, LED1.anode, SG1.2
  N2: Part1.D9, Part2.CE
  N3: Part1.D10, Part2.CS
  N4: Part1.D11/MOSI, Part2.MOSI
  N5: Part1.D12/MISO, Part2.MISO
  3V3: Part1.3V3, Part2.VCC
  N6: Part1.D13/SCK, Part2.SCK
